# Fritzing sketch circuit (saved by Fritzing 0.9.3b)
breadboards: 1

parts:
  KF-1 = KF-301 Relay [package=THT]
  WATER_PUMP1 = water pump/motor
  VCC2 = 4 x AAA Battery Mount
  부품1 = Arduino Uno (Rev3) - ICSP
  S1 = Pushbutton [package="[THT]"]

nets:
  N1: KF-1.signal, 부품1.D7
  N2: KF-1.power, 부품1.3V3
  N3: KF-1.ground, 부품1.GND, S1.Pin_1, S1.Pin_2
  N4: KF-1.C, VCC2.+
  N5: KF-1.NO, WATER_PUMP1.pin_2
  N6: WATER_PUMP1.pin_1, VCC2.-
  N7: 부품1.ICSP_MISO, 부품1.D12/MISO, S1.Pin_3, S1.Pin_4

custom parts:
  KF-301 Relay: KF-301
  water pump/motor: WATER PUMP BY ARDUBLOCKTR
